# Fritzing sketch ProjekatUS (saved by Fritzing 0.9.3b)
breadboards: 1

parts:
  LPC1114ETF1 = LPC1114ETF razvojni sistem
  Part1 = ETF Joystick
  Nokia_Display1 = Nokia Display
  Part2 = ETF Joystick

nets:
  N1: LPC1114ETF1.dp2, Nokia_Display1.DIN
  N2: LPC1114ETF1.dp4, Nokia_Display1.VCC
  N3: LPC1114ETF1.dp6, Nokia_Display1.CLK
  N4: LPC1114ETF1.dp9, Part1.SW
  N5: LPC1114ETF1.dp10, Part1.VRy
  N6: LPC1114ETF1.dp11, Part2.VRy
  N7: LPC1114ETF1.dp13, Part2.SW
  N8: LPC1114ETF1.dp18, Nokia_Display1.BL
  N9: LPC1114ETF1.dp23, Nokia_Display1.RST
  N10: LPC1114ETF1.dp24, Nokia_Display1.CE
  N11: LPC1114ETF1.dp25, Nokia_Display1.DC
  N12: LPC1114ETF1.GND#21, Nokia_Display1.GND
  GND: LPC1114ETF1.GND#22, Part1.GND, Part2.GND
  +5V: LPC1114ETF1.+3.3V, Part1.+5V, Part2.+5V
